# Fritzing sketch Modelo Arduino (saved by Fritzing 0.9.3b)
breadboards: 1

parts:
  Componente1 = Arduino Uno (Rev3)
  Componente2 = Bluetooth HC-05 Macho
  KY-1 = Keyes Relay [package=THT]
  LED3 = LEDs [package=led10mm]
  U3 = NodeMCU V1.0
  Componente3 = HC-SR501 Body Sensor Module

nets:
  N1: Componente1.D8, KY-1.signal
  N2: Componente1.D0/RX, U3.RX
  N3: Componente1.D1/TX, U3.TX
  N4: Componente1.D2, Componente2.RXD
  N5: Componente1.D3_PWM, Componente2.TXD
  N6: Componente1.D4, Componente3.VCC
  3V3: Componente1.3V3, U3.3V3
  5V: Componente1.5V, Componente2.VCC, KY-1.power, Componente3.OUT
  GND: Componente1.GND, Componente2.GND, KY-1.ground, U3.GND, Componente3.GND
  N7: KY-1.C, LED3.A
  N8: KY-1.NO, LED3.C

custom parts:
  Keyes Relay: The Keyes 5V relay module is suitable for SCM development, home appliance control. It uses a 5V~12V TIL control signal which can control DC / AC signal.
  LEDs: LEDs Standard schematic elements and footprints for 5mm, 3mm, 1206, and 0603 sized LEDs. 5mm - Spark Fun Electronics SKU : COM-00529 (and others)
  NodeMCU V1.0: ESP8266 based NodeMCU
  HC-SR501 Body Sensor Module: Pyroelectric Infrared PIR Motion Sensor Detector Module

// code stored in the sketch: Modelo.ino
#include<ESP8266WiFi.h>
#include<WiFiClient.h>
#include<ESP8266WebServer.h>
#include<ESP8266mDNS.h>
#includer <WiFi.h>

int receptorWifi = 0;
int transmisorWifi = 1;
int receptorBluetooth = 2
int transmisorBluetooth = 3;
int sensorMovimiento = 4;

char nombreWifi;
char password;


int Bombillo = 8; 

public bool movimiento; 


int estado = 0;

void setup(){

Serial.begin(9600);

pinMode(receptorWifi , INPUT); 
pinMode(transmisorWifi , OUTPUT); 
pinMode(receptorBluetooth , INPUT); 
pinMode(transmisorBluetooth , OUTPUT);
pinMode(sensorMovimiento , INPUT);
pinMode(Bombillo , OUTPUT);

ConnectWiFi();

}

void loop(){

	if(Serial.available() > 0 ){

		estado = Serial.read(); 

	}

	if(digitalRead(sensorMovimiento == HIGH){
		
			Serial.println("Se detecto Movimiento")
			digitalWrite(Bombillo, HIGH);
			movimiento = true;
		
		}

// A continuaci?n seg?n la informaci?n que recibimos via bluetooth enviamos voltaje por los puertos de arduino
	switch(estado){
	
		// Para en el caso que la variable sea  1 encenderemos Bombillo
		case 1: 
		digitalWrite(Bombillo, HIGH);
		break;

		// Para en el caso que la variable sea  2 apagaremos Bombillo
		case 2: 
		digitalWrite(Bombillo, LOW);
		break;


	}
}

void ConnectWiFi()
{
   Serial.println("");
   WiFi.mode(WIFI_STA);
   WiFi.begin(nombreWifi, password);
   while (WiFi.status() != WL_CONNECTED) 
   { 
     delay(100);  
     Serial.print('.'); 
   }
 
   Serial.println("");
   Serial.print("Iniciado STA:\t");
   Serial.println(nombreWifi);
   Serial.print("IP address:\t");
   Serial.println(WiFi.localIP());
}
